// Logisim project parallel.circ as structural Verilog: 7 circuits, main circuit computing_unit
module computing_unit (
  input  clk,
  input  [7:0] number,
  input  multiply,
  input  load_C,
  input  carry_in,
  input  divide,
  input  load_B,
  input  invert,
  input  load_A,
  input  add,
  input  reset_result,
  output mult_ready,
  output [15:0] Result,
  output div_ready
);

  wire and_1_out, and_2_out, or_1_out, or_2_out, or_3_out, shift_register_1_p4, shift_register_1_p14,
       shift_register_1_p15, shift_register_1_p16, shift_register_1_p17, shift_register_1_p18,
       shift_register_1_p19, shift_register_1_p20, shift_register_2_p8, shift_register_2_p9,
       shift_register_2_p10;
  wire [7:0] controlled8inverter_1_f;
  wire [15:0] adder_1_out, from8to16_1_x16, multiplexer_1_out, undriven;

  // Shift_Register shift_register_1: pin names not known; wires that end beside it: load_B, multiply, clk, shift_register_1_p4, number[7], number[6], number[5], number[4], number[3], number[2], number[1], number[0], shift_register_1_p4, shift_register_1_p14, shift_register_1_p15, shift_register_1_p16, shift_register_1_p17, shift_register_1_p18, shift_register_1_p19, shift_register_1_p20
  // Shift_Register #(.length(3)) shift_register_2: pin names not known; wires that end beside it: load_C, divide, clk, 1'b0, 1'b0, number[2], number[1], shift_register_2_p8, shift_register_2_p9, shift_register_2_p10
  nor nor_1 (mult_ready, shift_register_1_p4, shift_register_1_p14, shift_register_1_p15, shift_register_1_p16, shift_register_1_p17, shift_register_1_p18, shift_register_1_p19, shift_register_1_p20);
  and and_1 (and_1_out, shift_register_1_p20, multiply);
  or or_1 (or_1_out, shift_register_2_p8, shift_register_2_p9, shift_register_2_p10);
  or or_2 (or_2_out, and_1_out, add);
  not not_1 (div_ready, or_1_out);
  and and_2 (and_2_out, or_1_out, divide);
  // Shift_Register #(.length(16)) shift_register_3: pin names not known; wires that end beside it: load_A, multiply, clk, 1'b0
  // Shift_Register #(.length(16)) shift_register_4: pin names not known; wires that end beside it: reset_result, or_2_out, and_2_out, clk, adder_1_out[15]
  Multiplexer #(.width(16)) multiplexer_1 (.in0(undriven), .in1(from8to16_1_x16), .out(multiplexer_1_out), .sel(add));
  or or_3 (or_3_out, carry_in, invert);
  Adder #(.width(16)) adder_1 (.a(multiplexer_1_out), .b(Result), .out(adder_1_out), .cin(or_3_out));  // open: cout
  from8to16 from8to16_1 (.x8(controlled8inverter_1_f), .x16(from8to16_1_x16));
  controlled8inverter controlled8inverter_1 (.invert(invert), .x(number), .f(controlled8inverter_1_f));
endmodule

module number_loader (
  input  clk,
  input  reset,
  input  [7:0] number,
  input  load,
  input  [1:0] register_selector,
  output [7:0] x,
  output [7:0] y,
  output [7:0] z,
  output [7:0] t
);

  wire demultiplexer_1_out0, demultiplexer_1_out1, demultiplexer_1_out2, demultiplexer_1_out3;

  Demultiplexer #(.select(2)) demultiplexer_1 (
    .out0(demultiplexer_1_out0), .out1(demultiplexer_1_out1), .out2(demultiplexer_1_out2),
    .out3(demultiplexer_1_out3), .in(load), .sel(register_selector));
  Register register_1 (.D(number), .en(demultiplexer_1_out0), .clk(clk), .Q(x), .clr(reset));
  Register register_2 (.D(number), .en(demultiplexer_1_out1), .clk(clk), .Q(y), .clr(reset));
  Register register_3 (.D(number), .en(demultiplexer_1_out2), .clk(clk), .Q(z), .clr(reset));
  Register register_4 (.D(number), .en(demultiplexer_1_out3), .clk(clk), .Q(t), .clr(reset));
endmodule

module from8to16 (
  input  [7:0] x8,
  output [15:0] x16
);


  assign x16 = {{9{x8[7]}}, x8[6:0]};
endmodule

module controlled8inverter (
  input  invert,
  input  [7:0] x,
  output [7:0] f
);

  xor xor_1 (f[7], invert, x[7]);
  xor xor_2 (f[6], invert, x[6]);
  xor xor_3 (f[5], invert, x[5]);
  xor xor_4 (f[4], invert, x[4]);
  xor xor_5 (f[3], invert, x[3]);
  xor xor_6 (f[2], invert, x[2]);
  xor xor_7 (f[1], invert, x[1]);
  xor xor_8 (f[0], invert, x[0]);
endmodule

module data_path (
  input  clk,
  input  load_B,
  input  load_const,
  input  load_C,
  input  carry_in,
  input  load_A,
  input  [7:0] \const ,
  input  [7:0] number,
  input  divide,
  input  add,
  input  multiply,
  input  load,
  input  invert,
  input  reset_result,
  input  [1:0] register_selector,
  input  reset_input,
  output mult_ready,
  output [15:0] result,
  output div_ready
);

  wire [7:0] multiplexer_1_out, multiplexer_2_out, number_loader_1_t, number_loader_1_x, number_loader_1_y,
       number_loader_1_z;

  number_loader number_loader_1 (
    .clk(clk), .reset(reset_input), .number(number), .load(load), .register_selector(register_selector),
    .x(number_loader_1_x), .y(number_loader_1_y), .z(number_loader_1_z), .t(number_loader_1_t));
  Multiplexer #(.select(2), .width(8)) multiplexer_1 (
    .in0(number_loader_1_x), .in1(number_loader_1_y), .in2(number_loader_1_z), .in3(number_loader_1_t),
    .out(multiplexer_1_out), .sel(register_selector));
  Multiplexer #(.width(8)) multiplexer_2 (
    .in0(multiplexer_1_out), .in1(\const ), .out(multiplexer_2_out), .sel(load_const));
  computing_unit computing_unit_1 (
    .clk(clk), .number(multiplexer_2_out), .multiply(multiply), .load_C(load_C), .carry_in(carry_in),
    .divide(divide), .load_B(load_B), .invert(invert), .load_A(load_A), .add(add),
    .reset_result(reset_result), .mult_ready(mult_ready), .Result(result), .div_ready(div_ready));
endmodule

module sequencer (
  input  NR,
  input  ST,
  input  clk,
  input  reset_counter,
  input  in_5,
  input  in_6,
  input  in_7,
  input  in_8,
  input  in_9,
  output [1:0] register_selector,
  output load,
  output RDY,
  output RR
);

  wire comparator_1_eq, count_up, if_statement_1_false, if_statement_1_true, if_statement_2_false,
       if_statement_2_true, if_statement_3_false, if_statement_3_true, or_1_out, or_2_out, wait_NR_0_q;
  wire [1:0] count;

  Demultiplexer demultiplexer_1 (.out0(RR), .in(RR), .sel(ST));  // open: out1
  or or_1 (or_1_out, if_statement_1_true, count_up, in_9);
  assign register_selector = in_5 ? 2'b00 : 2'bz;  // Controlled_Buffer controlled_buffer_1
  assign register_selector = in_6 ? 2'b01 : 2'bz;  // Controlled_Buffer controlled_buffer_2
  assign register_selector = in_7 ? 2'b10 : 2'bz;  // Controlled_Buffer controlled_buffer_3
  assign register_selector = in_8 ? 2'b11 : 2'bz;  // Controlled_Buffer controlled_buffer_4
  assign register_selector = load ? count : 2'bz;  // Controlled_Buffer controlled_buffer_5
  D_Flip_Flop wait_NR_1 (.D(or_1_out), .clk(clk), .Q(RDY));  // open: Qn, preset, reset
  if_statement if_statement_1 (.condition(NR), .sgn(RDY), .False(if_statement_1_false), .True(if_statement_1_true));
  D_Flip_Flop load_current_register (.D(if_statement_1_false), .clk(clk), .Q(load));  // open: Qn, preset, reset
  or or_2 (or_2_out, load, wait_NR_0_q);
  D_Flip_Flop wait_NR_0 (.D(if_statement_2_false), .clk(clk), .Q(wait_NR_0_q));  // open: Qn, preset, reset
  Counter #(.max('h3), .width(2)) counter_1 (
    .clr(reset_counter), .up(1'b1), .count(count_up), .clk(clk), .Q(count));  // open: load, D, carry
  if_statement if_statement_2 (
    .condition(NR), .sgn(or_2_out), .False(if_statement_2_false), .True(if_statement_2_true));
  Comparator #(.width(2)) comparator_1 (.a(count), .b(2'b11), .eq(comparator_1_eq));  // open: gt, lt
  if_statement if_statement_3 (
    .condition(comparator_1_eq), .sgn(if_statement_2_true), .False(if_statement_3_false),
    .True(if_statement_3_true));
  D_Flip_Flop next_register (.D(if_statement_3_true), .clk(clk), .Q(count_up));  // open: Qn, preset, reset

  // Other names for the same wires on the sheet: load_counter = load; load_T = in_8; load_X = in_5; load_Y = in_6;
  //   load_Z = in_7; reset = reset_counter
endmodule

module if_statement (
  input  condition,
  input  sgn,
  output False,
  output True
);

  and and_1 (False, condition, sgn);
  and and_2 (True, sgn, ~condition);  // AND_Gate
endmodule
